// Logisim project RISC 32 BIT MAIN.circ as structural Verilog: 1 circuit, main circuit main
module main (
  input  [31:0] in_1,
  input  [31:0] in_2
);

  wire Arithmetic, Clock, CLR, EnRC, HALT, Logic;
  wire [7:0] Dest, O1, O2;
  wire [31:0] OP1, OP2, Result;

  Clock clock_1 (.out(Clock));
  RISC_32_BIT_ALU_main main_1 (.Clock(Clock), .Result(Result), .OP1(OP1), .OP2(OP2));  // open: OpeartionCode, in_1
  // RISC_32_BIT_DECODE_main main_2: pin names not known; wires that end beside it: in_2, Clock, CLR, HALT, Dest, O1, O2, Arithmetic, Logic
  xor xor_1 (EnRC, Arithmetic, Logic);
  // RISC_32_BIT_REGISTERS_main main_3: pin names not known; wires that end beside it: 1'b1, in_1, Dest[4:0], Dest[4:0], O1[4:0], O2[4:0], EnRC, CLR, Clock, OP1, OP2

  // Other names for the same wires on the sheet: RC[4:0] = Dest[4:0]; Input[31:0] = in_1; REG1[4:0] = O1[4:0];
  //   REG2[4:0] = O2[4:0]
endmodule
